# Fritzing sketch ArduinoPianoLed_Trives_Pelayo.ino (saved by Fritzing 0.9.6b)
breadboards: 1

parts:
  S1 = Pushbutton [package="[THT]"]
  S2 = Pushbutton [package="[THT]"]
  S3 = Pushbutton [package="[THT]"]
  S4 = Pushbutton [package="[THT]"]
  S5 = Pushbutton [package="[THT]"]
  Componente1 = Arduino Uno (Rev3)
  J1 = Piezo Speaker
  R1 = Resistor [tolerance=±5% power=0.25 resistance=220 package=THT]
  R2 = Resistor [tolerance=±5% power=0.25 resistance=1k package=THT]
  LED1 = LED - 5mm [color="Red (633nm)" current=0.030 package="5 mm [THT]"]
  R3 = Resistor [tolerance=±5% power=0.25 resistance=220 package=THT]
  R4 = Resistor [tolerance=±5% power=0.25 resistance=4.7k package=THT]
  R5 = Resistor [tolerance=±5% power=0.25 resistance=1M package=THT]
  R6 = Resistor [tolerance=±5% power=0.25 resistance=1k package=THT]

nets:
  N1: S1.Pin_1, S1.Pin_2, S2.Pin_1, S2.Pin_2, S3.Pin_1, S3.Pin_2, S4.Pin_1, S4.Pin_2, S5.Pin_1, S5.Pin_2, Componente1.A0, R6.Pin_1
  N2: S1.Pin_3, S1.Pin_4, Componente1.5V, R1.Pin_1, R2.Pin_1, R4.Pin_0
  N3: S2.Pin_3, S2.Pin_4, R1.Pin_0
  N4: S3.Pin_3, S3.Pin_4, R2.Pin_0
  N5: S4.Pin_3, S4.Pin_4, R4.Pin_1
  N6: S5.Pin_3, S5.Pin_4, R5.Pin_1
  N7: Componente1.D8, J1.pin2
  N8: Componente1.D6_PWM, R3.Pin_1
  N9: Componente1.GND, J1.pin1, LED1.cathode, R5.Pin_0, R6.Pin_0
  N10: LED1.anode, R3.Pin_0

// code stored in the sketch: PEC2.ino
  // Código creado por Pelayo Trives para la PEC2 de la asignatura Diseño de interacción del Grado en Multimedia de la UOC.
  
  int notas[] = {261,294,330,349,392}; // Declaramos una matriz con la que, posteriormente, podremos ayudarnos para represetar las notas de nuestro piano. La llamaremos notas y estará compuesta de 5 elementos, los cuales son las frecuencias de las notas DO, RE, MI, FA y SOL.
  const int pinAltavoz = 8; // Declaramos esta constante (pues no variará) que será el pin (del Arduino, el número 8) al que conectaremos el piezo (desde la protoboard).
  const int pinLed = 6; // Declaramos esta constante (pues no variará) que será el pin (del Arduino, el número 6) al que conectaremos el LED (desde la protoboard).

  void setup() {
  
  Serial.begin(9600); // Esta instrucción le indica al Arduino que inicie comunicación con el ordenador a una velocidad de 9600 bits por segundo.
  pinMode(pinLed, OUTPUT); // Con esta función vamos a configurar el modo de trabajo del pin utilizado para el LED, en este caso el 6, para que sea de entrada o salida.
  digitalWrite(pinLed, HIGH); // Iniciamos una función que servirá, al iniciar el programa, si el LED funciona. Con esto lo encenderemos.
  delay(2000); // Con esto establecemos que la duración del encendido del LED será 2000 ms.
  digitalWrite(pinLed, LOW); // Con esto el LED se apagará.
  
  }

  void loop() {
  
  int valorAnalogico = analogRead(A0); // Estableceremos una variable llamada valorAnalogico, la cual será el pin A0 de nuestro Arduino, que usaremos para almacenar el valor de dicha clavija (que en principio será 0).
  
  Serial.println(valorAnalogico); // Con esto podremos ver los valores para ajustar las comparativas del if mediante el monitor de serie.

  if (valorAnalogico > 5) { // Aseguramos la comparativa con 5 para evitar falsos positivos.
    digitalWrite(pinLed, HIGH); // Si el valor es superior a 5, el LED se encenderá.
   } else {
    digitalWrite(pinLed, LOW); // Y si no lo es, no se encenderá.
   }
  
  if(valorAnalogico >= 1015 && valorAnalogico <= 1025) { // Además de el LED encenderse, si el valor está entre 1015 y 1025...
    tone(pinAltavoz, notas[0]); // Tocaremos la nota DO (primer valor de la matriz), en parte posible porque el piezo está conectado al pin 8 de nuestro Arduino (pinAltavoz).
   }
   else if(valorAnalogico >= 995 && valorAnalogico <= 1005) { // Además de el LED encenderse, si el valor está entre 995 y 1005...
    tone(pinAltavoz, notas[1]); // Tocaremos RE
   }
   else if(valorAnalogico >= 505 && valorAnalogico <= 515) { // Además de el LED encenderse, si el valor está entre 505 y 515...
    tone(pinAltavoz, notas[2]); // Tocaremos MI
   }
   else if(valorAnalogico >= 690 && valorAnalogico <= 700) { // Además de el LED encenderse, si el valor está entre 690 y 700...
    tone(pinAltavoz, notas[3]); // Tocaremos FA
   }
   else if(valorAnalogico >= 5 && valorAnalogico <= 15) { // Además de el LED encenderse, si el valor está entre 5 y 15...
    tone(pinAltavoz, notas[4]); // Tocaremos SOL
   }
   else {
    noTone(pinAltavoz); // Parará la generación de pulsos, es decir, si esta función no estuviese, al pulsar cualquier botón, no se detendría una vez quitásemos el dedo.
   }
   
  }
